# Fritzing sketch arduino_client (saved by Fritzing 0.9.2b)
breadboards: 1
perfboards: 1

parts:
  Part1 = Arduino Uno (Rev3)  # not connected
  Part2 = Arduino Ethernet Shield (Rev3)
  LCD1 = LCD screen  # not connected
  LED1 = LED - 5mm [color="Red (633nm)" package="5 mm [THT]"]
  KEYPAD1 = Membrane Matrix Keypad
  R1 = Resistor [tolerance=±5% resistance=220 package=THT]

nets:
  N1: Part2.GND, R1.Pin_0
  N2: Part2.A2, KEYPAD1.4
  N3: Part2.A3, KEYPAD1.3
  N4: Part2.A4/SDA, KEYPAD1.2
  N5: Part2.A5/SCL, KEYPAD1.1
  N6: Part2.PWM_D3, LED1.anode
  N7: Part2.PWM_D5, KEYPAD1.5
  N8: Part2.PWM_D6, KEYPAD1.6
  N9: Part2.D7, KEYPAD1.7

custom parts:
  Membrane Matrix Keypad: Membrane Matrix 3x4 Keypad
